# Fritzing sketch UV_furnace_circuit (saved by Fritzing 0.9.2b)

parts:
  Bauteil1 = Arduino Mega 2560 (Rev3)
  THERMO1 = MAX31855 Breakout Board with Thermocouple
  Bauteil2 = Arduino Ethernet Shield (Rev3)
  LDD-1000H1 = MeanWell LDD-1000H
  LDD-1000H2 = MeanWell LDD-1000H
  LDD-1000H3 = MeanWell LDD-1000H

nets:
  5V: Bauteil1.5V, THERMO1.Vin
  GND: Bauteil1.GND, THERMO1.GND
  N1: Bauteil1.D47, THERMO1.CS
  N2: Bauteil1.D50, THERMO1.DO
  N3: Bauteil1.D52, THERMO1.CLK
  N4: Bauteil2.PWM_D5, LDD-1000H3.PWM_DIM
  N5: Bauteil2.PWM_D6, LDD-1000H2.PWM_DIM
  N6: Bauteil2.D7, LDD-1000H1.PWM_DIM

custom parts:
  MeanWell LDD-1000H: DC-DC Constant Current Step-Down LED drive
